# Fritzing sketch tetrachorder final inverted (saved by Fritzing 1.0.6)
circuit board: 27.2725cm x 11.4881cm

parts:
  Mod1 = Raspberry Pi Pico
  D4 = Diode [package=diode-1n4148]
  S4 = Cherry MX Keyswitch
  S3 = Cherry MX Keyswitch
  S2 = Cherry MX Keyswitch
  S1 = Cherry MX Keyswitch
  D3 = Diode [package=diode-1n4148]
  D2 = Diode [package=diode-1n4148]
  D1 = Diode [package=diode-1n4148]
  D5 = Diode [package=diode-1n4148]
  D6 = Diode [package=diode-1n4148]
  D7 = Diode [package=diode-1n4148]
  D8 = Diode [package=diode-1n4148]
  S5 = Cherry MX Keyswitch
  S6 = Cherry MX Keyswitch
  S7 = Cherry MX Keyswitch
  S8 = Cherry MX Keyswitch
  D9 = Diode [package=diode-1n4148]
  D10 = Diode [package=diode-1n4148]
  D11 = Diode [package=diode-1n4148]
  D12 = Diode [package=diode-1n4148]
  S9 = Cherry MX Keyswitch
  S10 = Cherry MX Keyswitch
  S11 = Cherry MX Keyswitch
  S12 = Cherry MX Keyswitch
  D13 = Diode [package=diode-1n4148]
  D14 = Diode [package=diode-1n4148]
  D15 = Diode [package=diode-1n4148]
  D16 = Diode [package=diode-1n4148]
  S13 = Cherry MX Keyswitch
  S14 = Cherry MX Keyswitch
  S15 = Cherry MX Keyswitch
  S16 = Cherry MX Keyswitch
  D17 = Diode [package=diode-1n4148]
  D18 = Diode [package=diode-1n4148]
  D19 = Diode [package=diode-1n4148]
  D20 = Diode [package=diode-1n4148]
  S17 = Cherry MX Keyswitch
  S18 = Cherry MX Keyswitch
  S19 = Cherry MX Keyswitch
  S20 = Cherry MX Keyswitch
  D21 = Diode [package=diode-1n4148]
  D22 = Diode [package=diode-1n4148]
  D23 = Diode [package=diode-1n4148]
  D24 = Diode [package=diode-1n4148]
  D25 = Diode [package=diode-1n4148]
  D26 = Diode [package=diode-1n4148]
  S22 = Taiway 100-SP-X-T1 SPDT Miniature Toggle Switch [part_number=100-SP-X-T1-0-0-B1-M2 package=THT]
  S21 = Taiway 100-SP-X-T1 SPDT Miniature Toggle Switch [part_number=100-SP-X-T1-0-0-B1-M2 package=THT]
  S26 = Taiway 100-SP-X-T1 SPDT Miniature Toggle Switch [part_number=100-SP-X-T1-0-0-B1-M2 package=THT]
  S25 = Taiway 100-SP-X-T1 SPDT Miniature Toggle Switch [part_number=100-SP-X-T1-0-0-B1-M2 package=THT]
  S24 = Taiway 100-SP-X-T1 SPDT Miniature Toggle Switch [part_number=100-SP-X-T1-0-0-B1-M2 package=THT]
  S23 = Taiway 100-SP-X-T1 SPDT Miniature Toggle Switch [part_number=100-SP-X-T1-0-0-B1-M2 package=THT]
  JP3 = Header 12 [package=1x12_machine-pin-header_lock.004]
  JP4 = Header 12 [package=1x12_machine-pin-header_lock.004]

nets:
  N1: Mod1.pin_7, S4.pin_3
  N2: Mod1.pin_9, S5.pin_3
  N3: Mod1.pin_10, S16.pin_3
  N4: Mod1.pin_11, S17.pin_3
  N5: Mod1.pin_21, D6.A, D17.A, D18.A, JP3.3, JP4.3
  N6: Mod1.pin_22, D7.A, D19.A, D26.A, JP3.4, JP4.4
  N7: Mod1.pin_24, D8.A, D9.A, D20.A, D25.A, JP3.6, JP4.6
  N8: Mod1.pin_25, D1.A, D10.A, D13.A, D24.A, JP3.7, JP4.7
  N9: Mod1.pin_26, D2.A, D11.A, D14.A, D23.A, JP3.8, JP4.8
  N10: Mod1.pin_27, D3.A, D12.A, D15.A, D21.A, JP3.9, JP4.9
  N11: Mod1.pin_29, D4.A, D5.A, D16.A, D22.A, JP3.11, JP4.11
  N12: D4.C, S4.pin_6, S4.pin_7, S4.pin_8
  N13: S4.pin_4, S3.pin_3
  N14: S3.pin_4, S2.pin_3
  N15: S3.pin_6, S3.pin_7, S3.pin_8, D3.C
  N16: S2.pin_4, S1.pin_3
  N17: S2.pin_6, S2.pin_7, S2.pin_8, D2.C
  N18: S1.pin_4, S8.pin_3
  N19: S1.pin_6, S1.pin_7, S1.pin_8, D1.C
  N20: D5.C, S5.pin_6, S5.pin_7, S5.pin_8
  N21: D6.C, S6.pin_6, S6.pin_7, S6.pin_8
  N22: D7.C, S7.pin_6, S7.pin_7, S7.pin_8
  N23: D8.C, S8.pin_6, S8.pin_7, S8.pin_8
  N24: S5.pin_4, S12.pin_3
  N25: S6.pin_3, S7.pin_4
  N26: S7.pin_3, S8.pin_4
  N27: D9.C, S9.pin_6, S9.pin_7, S9.pin_8
  N28: D10.C, S10.pin_6, S10.pin_7, S10.pin_8
  N29: D11.C, S11.pin_6, S11.pin_7, S11.pin_8
  N30: D12.C, S12.pin_6, S12.pin_7, S12.pin_8
  N31: S9.pin_3, S10.pin_4
  N32: S10.pin_3, S11.pin_4
  N33: S11.pin_3, S12.pin_4
  N34: D13.C, S13.pin_6, S13.pin_7, S13.pin_8
  N35: D14.C, S14.pin_6, S14.pin_7, S14.pin_8
  N36: D15.C, S15.pin_6, S15.pin_7, S15.pin_8
  N37: D16.C, S16.pin_6, S16.pin_7, S16.pin_8
  N38: S13.pin_3, S14.pin_4
  N39: S13.pin_4, S18.pin_4
  N40: S14.pin_3, S15.pin_4
  N41: S15.pin_3, S16.pin_4
  N42: D17.C, S17.pin_6, S17.pin_7, S17.pin_8
  N43: D18.C, S18.pin_6, S18.pin_7, S18.pin_8
  N44: D19.C, S19.pin_6, S19.pin_7, S19.pin_8
  N45: D20.C, S20.pin_6, S20.pin_7, S20.pin_8
  N46: S17.pin_4, S22.COM, S21.COM, S26.COM, S25.COM, S24.COM, S23.COM
  N47: S18.pin_3, S19.pin_4
  N48: S19.pin_3, S20.pin_4
  N49: D21.C, S21.L1
  N50: D22.C, S22.L1
  N51: D23.C, S23.L1
  N52: D24.C, S24.L1
  N53: D25.C, S25.L1
  N54: D26.C, S26.L1

custom parts:
  Raspberry Pi Pico: Raspberry Pi Pico. Based around the RP2040 microcontroller the Pico is a low cost microcontroller device bringing Raspberry Pi quality, cost, and easy of use to the microcontroller space. Jan 2021, Split part in to two versions: SMD (this one) and tht. This one is single sided and uses the castellation pads to solder the module to the board (no holes, other than for the USB connector!). The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
