# Fritzing sketch tetrachorder final (saved by Fritzing 1.0.6)
circuit board: 27.2725cm x 11.4881cm

parts:
  Mod1 = Raspberry Pi Pico
  D4 = Diode [package=diode-1n4148]
  S4 = Cherry MX Keyswitch
  S3 = Cherry MX Keyswitch
  S2 = Cherry MX Keyswitch
  S1 = Cherry MX Keyswitch
  D3 = Diode [package=diode-1n4148]
  D2 = Diode [package=diode-1n4148]
  D1 = Diode [package=diode-1n4148]
  D5 = Diode [package=diode-1n4148]
  D6 = Diode [package=diode-1n4148]
  D7 = Diode [package=diode-1n4148]
  D8 = Diode [package=diode-1n4148]
  S5 = Cherry MX Keyswitch
  S6 = Cherry MX Keyswitch
  S7 = Cherry MX Keyswitch
  S8 = Cherry MX Keyswitch
  D9 = Diode [package=diode-1n4148]
  D10 = Diode [package=diode-1n4148]
  D11 = Diode [package=diode-1n4148]
  D12 = Diode [package=diode-1n4148]
  S9 = Cherry MX Keyswitch
  S10 = Cherry MX Keyswitch
  S11 = Cherry MX Keyswitch
  S12 = Cherry MX Keyswitch
  D13 = Diode [package=diode-1n4148]
  D14 = Diode [package=diode-1n4148]
  D15 = Diode [package=diode-1n4148]
  D16 = Diode [package=diode-1n4148]
  S13 = Cherry MX Keyswitch
  S14 = Cherry MX Keyswitch
  S15 = Cherry MX Keyswitch
  S16 = Cherry MX Keyswitch
  D17 = Diode [package=diode-1n4148]
  D18 = Diode [package=diode-1n4148]
  D19 = Diode [package=diode-1n4148]
  D20 = Diode [package=diode-1n4148]
  S17 = Cherry MX Keyswitch
  S18 = Cherry MX Keyswitch
  S19 = Cherry MX Keyswitch
  S20 = Cherry MX Keyswitch
  D21 = Diode [package=diode-1n4148]
  D22 = Diode [package=diode-1n4148]
  D23 = Diode [package=diode-1n4148]
  D24 = Diode [package=diode-1n4148]
  D25 = Diode [package=diode-1n4148]
  D26 = Diode [package=diode-1n4148]
  S22 = Taiway 100-SP-X-T1 SPDT Miniature Toggle Switch [part_number=100-SP-X-T1-0-0-B1-M2 package=THT]
  S21 = Taiway 100-SP-X-T1 SPDT Miniature Toggle Switch [part_number=100-SP-X-T1-0-0-B1-M2 package=THT]
  S26 = Taiway 100-SP-X-T1 SPDT Miniature Toggle Switch [part_number=100-SP-X-T1-0-0-B1-M2 package=THT]
  S25 = Taiway 100-SP-X-T1 SPDT Miniature Toggle Switch [part_number=100-SP-X-T1-0-0-B1-M2 package=THT]
  S24 = Taiway 100-SP-X-T1 SPDT Miniature Toggle Switch [part_number=100-SP-X-T1-0-0-B1-M2 package=THT]
  S23 = Taiway 100-SP-X-T1 SPDT Miniature Toggle Switch [part_number=100-SP-X-T1-0-0-B1-M2 package=THT]

nets:
  N1: Mod1.pin_9, S4.pin_4
  N2: Mod1.pin_10, S3.pin_4
  N3: Mod1.pin_11, S2.pin_4
  N4: Mod1.pin_12, S1.pin_4
  N5: Mod1.pin_21, D23.A, D24.A, D25.A, D26.A
  N6: Mod1.pin_22, D21.A, D22.A
  N7: Mod1.pin_24, D17.A, D18.A, D19.A, D20.A
  N8: Mod1.pin_25, D13.A, D14.A, D15.A, D16.A
  N9: Mod1.pin_26, D9.A, D10.A, D11.A, D12.A
  N10: Mod1.pin_27, D5.A, D6.A, D7.A, D8.A
  N11: Mod1.pin_29, D4.A, D3.A, D2.A, D1.A
  N12: D4.C, S4.pin_9, S4.pin_10
  N13: S4.pin_6, S4.pin_8, S8.pin_4
  N14: S3.pin_1, S3.pin_9, S3.pin_10, D3.C
  N15: S3.pin_6, S3.pin_8, S7.pin_4
  N16: S2.pin_6, S2.pin_7, S6.pin_4
  N17: S2.pin_10, D2.C
  N18: S1.pin_1, S1.pin_10, D1.C
  N19: S1.pin_6, S1.pin_7, S5.pin_4
  N20: D5.C, S5.pin_1, S5.pin_10
  N21: D6.C, S6.pin_1, S6.pin_10
  N22: D7.C, S7.pin_1, S7.pin_10
  N23: D8.C, S8.pin_1, S8.pin_9, S8.pin_10
  N24: S5.pin_6, S5.pin_7, S9.pin_4
  N25: S6.pin_6, S6.pin_8, S10.pin_4
  N26: S7.pin_6, S7.pin_8, S11.pin_4
  N27: S8.pin_6, S8.pin_7, S12.pin_4
  N28: D9.C, S9.pin_1, S9.pin_10
  N29: D10.C, S10.pin_1, S10.pin_10
  N30: D11.C, S11.pin_1, S11.pin_10
  N31: D12.C, S12.pin_1, S12.pin_10
  N32: S9.pin_6, S9.pin_8, S13.pin_4
  N33: S10.pin_6, S10.pin_8, S14.pin_4
  N34: S11.pin_6, S11.pin_8, S15.pin_4
  N35: S12.pin_6, S12.pin_8, S16.pin_4
  N36: D13.C, S13.pin_1, S13.pin_10
  N37: D14.C, S14.pin_1, S14.pin_10
  N38: D15.C, S15.pin_1, S15.pin_10
  N39: D16.C, S16.pin_1, S16.pin_10
  N40: S13.pin_6, S13.pin_7, S13.pin_8, S17.pin_4
  N41: S14.pin_6, S14.pin_8, S18.pin_4
  N42: S15.pin_6, S15.pin_7, S15.pin_8, S19.pin_4
  N43: S16.pin_6, S16.pin_7, S16.pin_8, S20.pin_4
  N44: D17.C, S17.pin_1, S17.pin_10
  N45: D18.C, S18.pin_1, S18.pin_10
  N46: D19.C, S19.pin_1, S19.pin_10
  N47: D20.C, S20.pin_1, S20.pin_10
  N48: S17.pin_6, S17.pin_7, S21.COM, S23.COM
  N49: S18.pin_6, S18.pin_7, S22.COM, S24.COM
  N50: S19.pin_6, S19.pin_7, S25.COM
  N51: S20.pin_6, S20.pin_7, S26.COM
  N52: D21.C, S21.L2
  N53: D22.C, S22.L2
  N54: D23.C, S23.L2
  N55: D24.C, S24.L2
  N56: D25.C, S25.L2
  N57: D26.C, S26.L2

custom parts:
  Raspberry Pi Pico: Raspberry Pi Pico. Based around the RP2040 microcontroller the Pico is a low cost microcontroller device bringing Raspberry Pi quality, cost, and easy of use to the microcontroller space. Jan 2021, Split part in to two versions: SMD (this one) and tht. This one is single sided and uses the castellation pads to solder the module to the board (no holes, other than for the USB connector!). The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
