# Fritzing sketch tetrachorder matrix kbd2 (saved by Fritzing 1.0.6)

parts:
  D1 = Diode [package=diode-1n4148]
  Mod1 = Raspberry Pi Pico
  S1 = Pushbutton [package="[THT]"]
  D2 = Diode [package=diode-1n4148]
  S2 = Pushbutton [package="[THT]"]
  D3 = Diode [package=diode-1n4148]
  D4 = Diode [package=diode-1n4148]
  S3 = Pushbutton [package="[THT]"]
  S4 = Pushbutton [package="[THT]"]
  D5 = Diode [package=diode-1n4148]
  D6 = Diode [package=diode-1n4148]
  D7 = Diode [package=diode-1n4148]
  S6 = Pushbutton [package="[THT]"]
  D8 = Diode [package=diode-1n4148]
  D10 = Diode [package=diode-1n4148]
  D11 = Diode [package=diode-1n4148]
  D12 = Diode [package=diode-1n4148]
  D13 = Diode [package=diode-1n4148]
  D14 = Diode [package=diode-1n4148]
  S9 = Pushbutton [package="[THT]"]
  S10 = Pushbutton [package="[THT]"]
  S11 = Pushbutton [package="[THT]"]
  S14 = Pushbutton [package="[THT]"]
  S15 = Pushbutton [package="[THT]"]
  D15 = Diode [package=diode-1n4148]
  D16 = Diode [package=diode-1n4148]
  D17 = Diode [package=diode-1n4148]
  D18 = Diode [package=diode-1n4148]
  D19 = Diode [package=diode-1n4148]
  D20 = Diode [package=diode-1n4148]
  D21 = Diode [package=diode-1n4148]
  S16 = Pushbutton [package="[THT]"]
  S17 = Pushbutton [package="[THT]"]
  S19 = Pushbutton [package="[THT]"]
  S20 = Pushbutton [package="[THT]"]
  S21 = Pushbutton [package="[THT]"]
  D22 = Diode [package=diode-1n4148]
  D23 = Diode [package=diode-1n4148]
  D25 = Diode [package=diode-1n4148]
  D26 = Diode [package=diode-1n4148]
  D27 = Diode [package=diode-1n4148]
  D28 = Diode [package=diode-1n4148]
  S23 = Pushbutton [package="[THT]"]
  S24 = Pushbutton [package="[THT]"]
  S26 = Pushbutton [package="[THT]"]
  S27 = Pushbutton [package="[THT]"]
  S28 = Pushbutton [package="[THT]"]
  D24 = Diode [package=diode-1n4148]
  S30 = Taiway 100-SP-X-T1 SPDT Miniature Toggle Switch [part_number=100-SP-X-T1-0-0-B1-M1 package=THT]
  S31 = Taiway 100-SP-X-T1 SPDT Miniature Toggle Switch [part_number=100-SP-X-T1-0-0-B1-M1 package=THT]
  D9 = Diode [package=diode-1n4148]
  S32 = Taiway 100-SP-X-T1 SPDT Miniature Toggle Switch [part_number=100-SP-X-T1-0-0-B1-M1 package=THT]
  S33 = Taiway 100-SP-X-T1 SPDT Miniature Toggle Switch [part_number=100-SP-X-T1-0-0-B1-M1 package=THT]
  S34 = Taiway 100-SP-X-T1 SPDT Miniature Toggle Switch [part_number=100-SP-X-T1-0-0-B1-M1 package=THT]
  S35 = Taiway 100-SP-X-T1 SPDT Miniature Toggle Switch [part_number=100-SP-X-T1-0-0-B1-M1 package=THT]
  S36 = Taiway 100-SP-X-T1 SPDT Miniature Toggle Switch [part_number=100-SP-X-T1-0-0-B1-M1 package=THT]
  S37 = Taiway 100-SP-X-T1 SPDT Miniature Toggle Switch [part_number=100-SP-X-T1-0-0-B1-M1 package=THT]

nets:
  N1: D1.A, S1.Pin_3, S1.Pin_4, S2.Pin_1, S2.Pin_2
  N2: D1.C, Mod1.pin_29, D10.C, D18.C, D25.C
  N3: Mod1.pin_7, S1.Pin_1, S1.Pin_2
  N4: Mod1.pin_9, S9.Pin_1, S9.Pin_2
  N5: Mod1.pin_10, S16.Pin_1, S16.Pin_2
  N6: Mod1.pin_11, S23.Pin_1, S23.Pin_2
  N7: Mod1.pin_21, D7.C, D11.C, D17.C, D24.C
  N8: Mod1.pin_22, D5.C, D19.C, D26.C, D9.C
  N9: Mod1.pin_24, D6.C, D12.C, D21.C, D28.C
  N10: Mod1.pin_25, D3.C, D8.C, D20.C, D27.C
  N11: Mod1.pin_26, D4.C, D13.C, D15.C, D22.C
  N12: Mod1.pin_27, D2.C
  N13: D2.A, S2.Pin_3, S2.Pin_4, S3.Pin_1, S3.Pin_2
  N14: D3.A, S4.Pin_3, S4.Pin_4, S6.Pin_1, S6.Pin_2
  N15: D4.A, S3.Pin_3, S3.Pin_4, S4.Pin_1, S4.Pin_2
  N16: D5.A, S30.L1
  N17: D6.A, S6.Pin_3, S6.Pin_4, S30.COM, S37.COM
  N18: D7.A, S37.L1
  N19: D8.A, S10.Pin_3, S10.Pin_4, S14.Pin_1, S14.Pin_2
  N20: D10.A, S9.Pin_3, S9.Pin_4, S11.Pin_1, S11.Pin_2
  N21: D11.A, S36.L1
  N22: D12.A, S14.Pin_3, S14.Pin_4, S31.COM, S36.COM
  N23: D13.A, S10.Pin_1, S10.Pin_2, S15.Pin_3, S15.Pin_4
  N24: D14.A, S11.Pin_3, S11.Pin_4, S15.Pin_1, S15.Pin_2
  N25: D14.C, D16.C, D23.C
  N26: D15.A, S19.Pin_1, S19.Pin_2, S20.Pin_3, S20.Pin_4
  N27: D16.A, S20.Pin_1, S20.Pin_2, S21.Pin_3, S21.Pin_4
  N28: D17.A, S35.L1
  N29: D18.A, S16.Pin_3, S16.Pin_4, S21.Pin_1, S21.Pin_2
  N30: D19.A, S32.L1
  N31: D20.A, S17.Pin_1, S17.Pin_2, S19.Pin_3, S19.Pin_4
  N32: D21.A, S17.Pin_3, S17.Pin_4, S32.COM, S35.COM
  N33: D22.A, S26.Pin_1, S26.Pin_2, S27.Pin_3, S27.Pin_4
  N34: D23.A, S27.Pin_1, S27.Pin_2, S28.Pin_3, S28.Pin_4
  N35: D25.A, S23.Pin_3, S23.Pin_4, S28.Pin_1, S28.Pin_2
  N36: D26.A, S33.L1
  N37: D27.A, S24.Pin_1, S24.Pin_2, S26.Pin_3, S26.Pin_4
  N38: D28.A, S24.Pin_3, S24.Pin_4, S33.COM, S34.COM
  N39: D24.A, S34.L1
  N40: S31.L1, D9.A

notes:
  Rows: GPIO 22, 21, 20, 19, 18, 17, 16: OUT (activator)
  level is LOW in nominal mode
  level is HIGH when polling kbd
  Columns: GPIO 5, 6 7, 8: IN (actived)
  When polling kbd, HIGH means key is pressed
  diode direction is WRONG in this diagram.
  diode should be placed so current goes from activator to activated
  On the diagram, the diodes are the other way round!

custom parts:
  Raspberry Pi Pico: Raspberry Pi Pico. Based around the RP2040 microcontroller the Pico is a low cost microcontroller device bringing Raspberry Pi quality, cost, and easy of use to the microcontroller space. Jan 2021, Split part in to two versions: SMD (this one) and tht. This one is single sided and uses the castellation pads to solder the module to the board (no holes, other than for the USB connector!). The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
