# Fritzing sketch tetrachorder matrix kbd4 (saved by Fritzing 1.0.6)
breadboards: 3

parts:
  Mod1 = Raspberry Pi Pico
  S38 = Pushbutton [package="[THT]"]
  D29 = Diode [package=diode-1n4148]
  D30 = Diode [package=diode-1n4148]
  S39 = Pushbutton [package="[THT]"]
  D31 = Diode [package=diode-1n4148]
  S40 = Pushbutton [package="[THT]"]
  D32 = Diode [package=diode-1n4148]
  S41 = Pushbutton [package="[THT]"]
  D33 = Diode [package=diode-1n4148]
  S42 = Pushbutton [package="[THT]"]
  D34 = Diode [package=diode-1n4148]
  S43 = Pushbutton [package="[THT]"]
  D35 = Diode [package=diode-1n4148]
  S44 = Pushbutton [package="[THT]"]
  D36 = Diode [package=diode-1n4148]
  D37 = Diode [package=diode-1n4148]
  D38 = Diode [package=diode-1n4148]
  D39 = Diode [package=diode-1n4148]
  D40 = Diode [package=diode-1n4148]
  D41 = Diode [package=diode-1n4148]
  D42 = Diode [package=diode-1n4148]
  S45 = Pushbutton [package="[THT]"]
  S46 = Pushbutton [package="[THT]"]
  S47 = Pushbutton [package="[THT]"]
  S48 = Pushbutton [package="[THT]"]
  S49 = Pushbutton [package="[THT]"]
  S50 = Pushbutton [package="[THT]"]
  S51 = Pushbutton [package="[THT]"]
  D43 = Diode [package=diode-1n4148]
  D44 = Diode [package=diode-1n4148]
  D45 = Diode [package=diode-1n4148]
  D46 = Diode [package=diode-1n4148]
  D47 = Diode [package=diode-1n4148]
  D48 = Diode [package=diode-1n4148]
  D49 = Diode [package=diode-1n4148]
  D50 = Diode [package=diode-1n4148]
  D51 = Diode [package=diode-1n4148]
  D52 = Diode [package=diode-1n4148]
  D53 = Diode [package=diode-1n4148]
  D54 = Diode [package=diode-1n4148]
  D55 = Diode [package=diode-1n4148]
  D56 = Diode [package=diode-1n4148]
  S52 = Pushbutton [package="[THT]"]
  S53 = Pushbutton [package="[THT]"]
  S54 = Pushbutton [package="[THT]"]
  S55 = Pushbutton [package="[THT]"]
  S56 = Pushbutton [package="[THT]"]
  S57 = Pushbutton [package="[THT]"]
  S58 = Pushbutton [package="[THT]"]
  S59 = Pushbutton [package="[THT]"]
  S60 = Pushbutton [package="[THT]"]
  S61 = Pushbutton [package="[THT]"]
  S62 = Pushbutton [package="[THT]"]
  S63 = Pushbutton [package="[THT]"]
  S64 = Pushbutton [package="[THT]"]
  S65 = Pushbutton [package="[THT]"]
  S66 = Taiway 100-SP-X-T1 SPDT Miniature Toggle Switch [part_number=100-SP-X-T1-0-0-B1-M1 package=THT]  # not connected

nets:
  N1: Mod1.pin_3, Mod1.pin_8, Mod1.pin_13, Mod1.pin_18, Mod1.pin_23, Mod1.pin_28, Mod1.pin_33, Mod1.pin_38
  N2: Mod1.pin_7, S38.Pin_1, S38.Pin_2, S38.Pin_3, S38.Pin_4, D29.A, D30.A, S39.Pin_1, S39.Pin_2, S39.Pin_3, S39.Pin_4, D31.A, S40.Pin_1, S40.Pin_2, S40.Pin_3, S40.Pin_4, D32.A, S41.Pin_1, S41.Pin_2, S41.Pin_3, S41.Pin_4, D33.A, S42.Pin_1, S42.Pin_2, S42.Pin_3, S42.Pin_4, D34.A, S43.Pin_1, S43.Pin_2, S43.Pin_3, S43.Pin_4, D35.A, S44.Pin_1, S44.Pin_2, S44.Pin_3, S44.Pin_4
  N3: Mod1.pin_9, D36.A, D37.A, D38.A, D39.A, D40.A, D41.A, D42.A, S45.Pin_1, S45.Pin_2, S46.Pin_1, S46.Pin_2, S47.Pin_1, S47.Pin_2, S48.Pin_1, S48.Pin_2, S49.Pin_1, S49.Pin_2, S50.Pin_1, S50.Pin_2, S51.Pin_1, S51.Pin_2
  N4: Mod1.pin_10, D45.A, D48.A, D49.A, D50.A, D51.A, D54.A, D55.A, S53.Pin_1, S53.Pin_2, S53.Pin_3, S53.Pin_4, S54.Pin_1, S54.Pin_2, S54.Pin_3, S54.Pin_4, S55.Pin_1, S55.Pin_2, S55.Pin_3, S55.Pin_4, S56.Pin_1, S56.Pin_2, S56.Pin_3, S56.Pin_4, S57.Pin_1, S57.Pin_2, S57.Pin_3, S57.Pin_4, S61.Pin_1, S61.Pin_2, S61.Pin_3, S61.Pin_4, S63.Pin_1, S63.Pin_2, S63.Pin_3, S63.Pin_4
  N5: Mod1.pin_11, D43.A, D44.A, D46.A, D47.A, D52.A, D53.A, D56.A, S52.Pin_1, S52.Pin_2, S58.Pin_1, S58.Pin_2, S59.Pin_1, S59.Pin_2, S60.Pin_1, S60.Pin_2, S62.Pin_1, S62.Pin_2, S64.Pin_1, S64.Pin_2, S65.Pin_1, S65.Pin_2
  N6: Mod1.pin_21, D35.C, D37.C
  N7: Mod1.pin_22, D34.C, D39.C
  N8: Mod1.pin_24, D33.C, D36.C
  N9: Mod1.pin_25, D32.C, D40.C
  N10: Mod1.pin_26, D31.C, D38.C
  N11: Mod1.pin_27, D30.C, D42.C
  N12: Mod1.pin_29, D29.C, D41.C
  N13: D43.C, D50.C
  N14: D44.C, D48.C
  N15: D45.C, D56.C
  N16: D46.C, D54.C
  N17: D47.C, D55.C
  N18: D49.C, D52.C
  N19: D51.C, D53.C

notes:
  Rows: GPIO 22, 21, 20, 19, 18, 17, 16: OUT (activator)
  level is LOW in nominal mode
  level is HIGH when polling kbd
  Columns: GPIO 5, 6 7, 8: IN (actived)
  When polling kbd, HIGH means key is pressed
  diode direction is WRONG in this diagram.
  diode should be placed so current goes from activator to activated
  On the diagram, the diodes are the other way round!

custom parts:
  Raspberry Pi Pico: Raspberry Pi Pico. Based around the RP2040 microcontroller the Pico is a low cost microcontroller device bringing Raspberry Pi quality, cost, and easy of use to the microcontroller space. Jan 2021, Split part in to two versions: SMD (this one) and tht. This one is single sided and uses the castellation pads to solder the module to the board (no holes, other than for the USB connector!). The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
